// Logisim project cr8.circ as structural Verilog: 9 circuits, main circuit core
module main (
);

  wire clock_1_out, ctrl_1_dr_dev, ctrl_1_dr_f, ctrl_1_dr_io, ctrl_1_dr_k, ctrl_1_dr_lhs, ctrl_1_dr_mem,
       ctrl_1_dr_rhs, ctrl_1_dr_sel, ctrl_1_dw_sel, ctrl_1_fetch, ctrl_1_pc_inc, ctrl_1_pc_jmp,
       ctrl_1_pc_jnz, ctrl_1_sp_dec, ctrl_1_sp_inc;
  wire [1:0] ctrl_1_aw;
  wire [2:0] ctrl_1_alu_op, ctrl_1_dw;
  wire [7:0] controlled_buffer_1_out, core_1_mem_out, OP_q;

  Register OP (.D(core_1_mem_out), .en(ctrl_1_fetch), .clk(clock_1_out), .Q(OP_q), .clr(1'b0));
  byte_display byte_display_1 (.in_1(OP_q));
  assign controlled_buffer_1_out = 1'b0 ? 8'h2 : 8'bz;  // Controlled_Buffer controlled_buffer_1
  Clock clock_1 (.out(clock_1_out));
  core core_1 (
    .DW(ctrl_1_dw), .AW(ctrl_1_aw), .OP(OP_q), .CLK(clock_1_out), .DR_K(ctrl_1_dr_k), .DR_F(ctrl_1_dr_f),
    .DR_IO(ctrl_1_dr_io), .DR_MEM(ctrl_1_dr_mem), .DR_LHS(ctrl_1_dr_lhs), .DR_RHS(ctrl_1_dr_rhs),
    .DR_DEV(ctrl_1_dr_dev), .DR_SEL(ctrl_1_dr_sel), .DB_in(controlled_buffer_1_out), .DW_SEL(ctrl_1_dw_sel),
    .PC_JNZ(ctrl_1_pc_jnz), .PC_J(ctrl_1_pc_jmp), .PC_INC(ctrl_1_pc_inc), .ALU_OP(ctrl_1_alu_op),
    .SP_INC(ctrl_1_sp_inc), .SP_DEC(ctrl_1_sp_dec), .RST(1'b0), .MEM_out(core_1_mem_out));  // open: AB_in
  ctrl ctrl_1 (
    .RST(1'b0), .CLK(clock_1_out), .OP(OP_q[7:3]), .FETCH(ctrl_1_fetch), .PC_JMP(ctrl_1_pc_jmp),
    .DR_DEV(ctrl_1_dr_dev), .DR_RHS(ctrl_1_dr_rhs), .DR_LHS(ctrl_1_dr_lhs), .DR_MEM(ctrl_1_dr_mem),
    .DR_IO(ctrl_1_dr_io), .DR_F(ctrl_1_dr_f), .DR_K(ctrl_1_dr_k), .PC_JNZ(ctrl_1_pc_jnz),
    .DW_SEL(ctrl_1_dw_sel), .DR_SEL(ctrl_1_dr_sel), .SP_DEC(ctrl_1_sp_dec), .SP_INC(ctrl_1_sp_inc),
    .AW(ctrl_1_aw), .DW(ctrl_1_dw), .ALU_OP(ctrl_1_alu_op), .PC_INC(ctrl_1_pc_inc));
endmodule

module core (
  input  CLK,
  input  [7:0] DB_in,
  input  [15:0] AB_in,
  input  [2:0] DW,
  input  [1:0] AW,
  input  [7:0] OP,
  input  DR_K,
  input  DR_F,
  input  DR_IO,
  input  DR_MEM,
  input  DR_LHS,
  input  DR_RHS,
  input  DR_DEV,
  input  DR_SEL,
  input  DW_SEL,
  input  PC_JNZ,
  input  PC_J,
  input  PC_INC,
  input  [2:0] ALU_OP,
  input  SP_INC,
  input  SP_DEC,
  input  RST,
  output [7:0] MEM_out
);

  wire ALU_SEL_A, ALU_SEL_B, ALU_SEL_C, ALU_SEL_D, ALU_SEL_F, ALU_SEL_X, ALU_SEL_Y, ALU_SEL_Z, and_1_out,
       and_2_out, and_3_out, and_4_out, and_5_out, AR_PC, AR_SP, AW_LR, AW_PC, AW_SP, AW_XY, comparator_1_eq,
       comparator_2_eq, demultiplexer_5_out7, DR_A, DR_B, DR_C, DR_D, DR_F_t, DR_X, DR_Y, DR_Z, DW_A, DW_AF,
       DW_ALU, DW_B, DW_C, DW_D, DW_DEV, DW_F, DW_IO, DW_K, DW_MEM, DW_OP, DW_RHS, DW_X, DW_Y, DW_Z,
       not_1_out, not_2_out, not_3_out, or_3_out;
  wire [2:0] DR, DW_t;
  wire [7:0] A_q, alu_1_f, alu_1_q, ALUB, B_q, C_q, controlled_buffer_19_out, controlled_buffer_26_out,
       controlled_buffer_27_out, D_q, dev_kb_1_miso, dev_rng_1_miso, F_q, IO_q, K_q, X_q, Y_q, Z_q;
  wire [7:3] LHS_q;
  wire [9:0] SP_q;
  wire [15:0] PC_q;
  wire [15:11] RHS_q;

  assign DB_in = DW_OP ? OP : 8'bz;  // Controlled_Buffer controlled_buffer_1
  Demultiplexer #(.select(3)) demultiplexer_1 (
    .out0(ALU_SEL_A), .out1(ALU_SEL_B), .out2(ALU_SEL_C), .out3(ALU_SEL_D), .out4(ALU_SEL_X),
    .out5(ALU_SEL_Y), .out6(ALU_SEL_Z), .out7(ALU_SEL_F), .in(1'b1), .sel(DR));
  Demultiplexer #(.select(3)) demultiplexer_2 (
    .out0(DW_A), .out1(DW_B), .out2(DW_C), .out3(DW_D), .out4(DW_X), .out5(DW_Y), .out6(DW_Z), .out7(DW_F),
    .in(DW_SEL), .sel(DW_t));
  Demultiplexer #(.select(2)) demultiplexer_3 (
    .out0(AW_PC), .out1(AW_SP), .out2(AW_XY), .out3(AW_LR), .in(1'b1), .sel(AW));
  not not_1 (not_1_out, DW_SEL);
  Demultiplexer #(.select(3)) demultiplexer_4 (
    .out0(DW_MEM), .out1(DW_OP), .out2(DW_ALU), .out3(DW_AF), .out4(DW_K), .out5(DW_IO), .out6(DW_DEV),
    .out7(DW_RHS), .in(not_1_out), .sel(DW));
  Demultiplexer #(.select(3)) demultiplexer_5 (
    .out0(DR_A), .out1(DR_B), .out2(DR_C), .out3(DR_D), .out4(DR_X), .out5(DR_Y), .out6(DR_Z),
    .out7(demultiplexer_5_out7), .in(DR_SEL), .sel(DR));
  or or_1 (DR_F_t, demultiplexer_5_out7, DR_F);
  Register F (.D(DB_in), .en(DR_F_t), .clk(CLK), .Q(F_q), .clr(RST));
  LED led_1 (.in(DR_F_t));
  _7_Segment_Display u_7_segment_display_1 ();  // open: g, f, a, b, e, d, c, dp
  // BCD_to_7_Segment_decoder bcd_to_7_segment_decoder_1: pin names not known
  // Binary_to_BCD_converter #(.binvalue(8)) binary_to_bcd_converter_1: pin names not known; wires that end beside it: DR_K, DB_in
  Register A (.D(DB_in), .en(DR_A), .clk(CLK), .Q(A_q), .clr(RST));
  LED led_2 (.in(DR_A));
  Register K (.D(DB_in), .en(DR_K), .clk(CLK), .Q(K_q), .clr(RST));
  LED led_3 (.in(DR_K));
  Register LHS (.D(DB_in), .en(DR_LHS), .clk(CLK), .Q({LHS_q, DR}), .clr(RST));
  LED led_4 (.in(DR_LHS));
  byte_display byte_display_1 (.in_1(F_q));
  _7_Segment_Display u_7_segment_display_2 ();  // open: g, f, a, b, e, d, c, dp
  _7_Segment_Display u_7_segment_display_3 ();  // open: g, f, a, b, e, d, c, dp
  // BCD_to_7_Segment_decoder bcd_to_7_segment_decoder_2: pin names not known
  // BCD_to_7_Segment_decoder bcd_to_7_segment_decoder_3: pin names not known
  byte_display byte_display_2 (.in_1(A_q));
  LED led_5 (.in(DW_A));
  assign DB_in = DW_A ? A_q : 8'bz;  // Controlled_Buffer controlled_buffer_2
  assign ALUB = ALU_SEL_A ? A_q : 8'bz;  // Controlled_Buffer controlled_buffer_3
  byte_display byte_display_3 (.in_1(K_q));
  LED led_6 (.in(DW_K));
  assign DB_in = DW_K ? K_q : 8'bz;  // Controlled_Buffer controlled_buffer_4
  byte_display byte_display_4 (.in_1({LHS_q, DR}));
  LED led_7 (.in(DW_F));
  assign DB_in = DW_F ? F_q : 8'bz;  // Controlled_Buffer controlled_buffer_5
  assign AB_in = AW_LR ? {RHS_q, DW_t, LHS_q, DR} : 16'bz;  // Controlled_Buffer controlled_buffer_6
  Hex_Digit_Display #(.decimalPoint("false")) hex_digit_display_1 (.value(AB_in[15:12]));
  Register B (.D(DB_in), .en(DR_B), .clk(CLK), .Q(B_q), .clr(RST));
  LED led_8 (.in(DR_B));
  Register X (.D(DB_in), .en(DR_X), .clk(CLK), .Q(X_q), .clr(RST));
  LED led_9 (.in(DR_X));
  Register RHS (.D(DB_in), .en(DR_RHS), .clk(CLK), .Q({RHS_q, DW_t}), .clr(RST));
  LED led_10 (.in(DR_RHS));
  assign DB_in = DW_ALU ? alu_1_q : 8'bz;  // Controlled_Buffer controlled_buffer_7
  Hex_Digit_Display #(.decimalPoint("false")) hex_digit_display_2 (.value(AB_in[11:8]));
  Hex_Digit_Display #(.decimalPoint("false")) hex_digit_display_3 (.value(AB_in[7:4]));
  byte_display byte_display_5 (.in_1(B_q));
  LED led_11 (.in(DW_B));
  assign DB_in = DW_B ? B_q : 8'bz;  // Controlled_Buffer controlled_buffer_8
  assign ALUB = ALU_SEL_B ? B_q : 8'bz;  // Controlled_Buffer controlled_buffer_9
  byte_display byte_display_6 (.in_1(X_q));
  LED led_12 (.in(DW_X));
  assign DB_in = DW_X ? X_q : 8'bz;  // Controlled_Buffer controlled_buffer_10
  assign ALUB = ALU_SEL_X ? X_q : 8'bz;  // Controlled_Buffer controlled_buffer_11
  assign AB_in = AW_XY ? {Y_q, X_q} : 16'bz;  // Controlled_Buffer controlled_buffer_12
  LED led_13 (.in(DW_RHS));
  byte_display byte_display_7 (.in_1({RHS_q, DW_t}));
  assign DB_in = DW_RHS ? {RHS_q, DW_t} : 8'bz;  // Controlled_Buffer controlled_buffer_13
  alu alu_1 (.A(ALUB), .B({RHS_q, DW_t}), .OP(ALU_OP), .F_in(F_q), .F(alu_1_f), .Q(alu_1_q));
  Hex_Digit_Display #(.decimalPoint("false")) hex_digit_display_4 (.value(AB_in[3:0]));
  Register C (.D(DB_in), .en(DR_C), .clk(CLK), .Q(C_q), .clr(RST));
  LED led_14 (.in(DR_C));
  Register Y (.D(DB_in), .en(DR_Y), .clk(CLK), .Q(Y_q), .clr(RST));
  LED led_15 (.in(DR_Y));
  assign DB_in = DW_AF ? alu_1_f : 8'bz;  // Controlled_Buffer controlled_buffer_14
  not not_2 (not_2_out, alu_1_f[5]);
  and and_1 (and_1_out, not_2_out, PC_JNZ);
  byte_display byte_display_8 (.in_1(C_q));
  LED led_16 (.in(DW_C));
  byte_display byte_display_9 (.in_1(Y_q));
  LED led_17 (.in(DW_Y));
  Register IO (.D(DB_in), .en(DR_IO), .clk(CLK), .Q(IO_q), .clr(RST));
  LED led_18 (.in(DR_IO));
  or or_2 (AR_PC, and_1_out, PC_J);
  assign DB_in = DW_C ? C_q : 8'bz;  // Controlled_Buffer controlled_buffer_15
  assign ALUB = ALU_SEL_C ? C_q : 8'bz;  // Controlled_Buffer controlled_buffer_16
  assign DB_in = DW_Y ? Y_q : 8'bz;  // Controlled_Buffer controlled_buffer_17
  assign ALUB = ALU_SEL_Y ? Y_q : 8'bz;  // Controlled_Buffer controlled_buffer_18
  byte_display byte_display_10 (.in_1(IO_q));
  assign controlled_buffer_19_out = and_2_out ? DB_in : 8'bz;  // Controlled_Buffer controlled_buffer_19
  Register D (.D(DB_in), .en(DR_D), .clk(CLK), .Q(D_q), .clr(RST));
  LED led_19 (.in(DR_D));
  Register Z (.D(DB_in), .en(DR_Z), .clk(CLK), .Q(Z_q), .clr(RST));
  LED led_20 (.in(DR_Z));
  LED led_21 (.in(DW_IO));
  assign DB_in = DW_IO ? IO_q : 8'bz;  // Controlled_Buffer controlled_buffer_20
  Comparator comparator_1 (.a(IO_q), .b(8'h1), .eq(comparator_1_eq));  // open: gt, lt
  and and_2 (and_2_out, DR_DEV, comparator_1_eq);
  and and_3 (and_3_out, comparator_1_eq, DW_DEV);
  byte_display byte_display_11 (.in_1(D_q));
  LED led_22 (.in(DW_D));
  assign DB_in = DW_D ? D_q : 8'bz;  // Controlled_Buffer controlled_buffer_21
  assign ALUB = ALU_SEL_D ? D_q : 8'bz;  // Controlled_Buffer controlled_buffer_22
  byte_display byte_display_12 (.in_1(Z_q));
  LED led_23 (.in(DW_Z));
  assign DB_in = DW_Z ? Z_q : 8'bz;  // Controlled_Buffer controlled_buffer_23
  assign ALUB = ALU_SEL_Z ? Z_q : 8'bz;  // Controlled_Buffer controlled_buffer_24
  assign DB_in = and_3_out ? dev_kb_1_miso : 8'bz;  // Controlled_Buffer controlled_buffer_25
  dev_kb dev_kb_1 (
    .CLK(CLK), .SEND(and_3_out), .RECV(and_2_out), .MOSI(controlled_buffer_19_out), .MISO(dev_kb_1_miso));
  assign controlled_buffer_26_out = and_4_out ? DB_in : 8'bz;  // Controlled_Buffer controlled_buffer_26
  Comparator comparator_2 (.a(IO_q), .b(8'h2), .eq(comparator_2_eq));  // open: gt, lt
  and and_4 (and_4_out, DR_DEV, comparator_2_eq);
  and and_5 (and_5_out, comparator_2_eq, DW_DEV);
  Counter #(.max('hffff), .width(16)) PC (
    .clr(RST), .load(AR_PC), .up(1'b1), .count(PC_INC), .clk(CLK), .D(AB_in), .Q(PC_q));  // open: carry
  dev_rng dev_rng_1 (
    .CLK(CLK), .SEND(and_5_out), .RECV(and_4_out), .MOSI(controlled_buffer_26_out), .MISO(dev_rng_1_miso));
  assign controlled_buffer_27_out = DR_MEM ? DB_in : 8'bz;  // Controlled_Buffer controlled_buffer_27
  assign DB_in = and_5_out ? dev_rng_1_miso : 8'bz;  // Controlled_Buffer controlled_buffer_28
  Hex_Digit_Display #(.decimalPoint("false")) hex_digit_display_5 (.value(PC_q[15:12]));
  Hex_Digit_Display #(.decimalPoint("false")) hex_digit_display_6 (.value(PC_q[11:8]));
  assign AB_in = AW_PC ? PC_q : 16'bz;  // Controlled_Buffer controlled_buffer_29
  Hex_Digit_Display #(.decimalPoint("false")) hex_digit_display_7 (.value(PC_q[7:4]));
  Hex_Digit_Display #(.decimalPoint("false")) hex_digit_display_8 (.value(PC_q[3:0]));
  mem mem_1 (.ADDR(AB_in), .WE(DR_MEM), .CLK(CLK), .D_in(controlled_buffer_27_out), .D_Out(MEM_out));
  Counter #(.max('h2ff), .width(10)) SP (
    .clr(RST), .load(AR_SP), .up(not_3_out), .count(or_3_out), .clk(CLK), .D(AB_in[9:0]), .Q(SP_q));  // open: carry
  not not_3 (not_3_out, SP_DEC);
  or or_3 (or_3_out, SP_DEC, SP_INC);
  assign DB_in = DW_MEM ? MEM_out : 8'bz;  // Controlled_Buffer controlled_buffer_30
  Hex_Digit_Display #(.decimalPoint("false")) hex_digit_display_9 (.value(4'b1111));
  Hex_Digit_Display #(.decimalPoint("false")) hex_digit_display_10 (.value({2'b11, SP_q[9:8]}));
  Hex_Digit_Display #(.decimalPoint("false")) hex_digit_display_11 (.value(SP_q[7:4]));
  Hex_Digit_Display #(.decimalPoint("false")) hex_digit_display_12 (.value(SP_q[3:0]));
  assign AB_in = AW_SP ? {{6{1'b1}}, SP_q} : 16'bz;  // Controlled_Buffer controlled_buffer_31

  // Other names for the same wires on the sheet: AB[15:0] = AB_in; ADDRBUS_WRITER[1:0] = AW; DATABUS_WRITER[2:0] = DW;
  //   DB[7:0] = DB_in; PCJ = PC_J; PCJNZ = PC_JNZ

  // Notes on the sheet:
  //   DATA BUS
  //   ADDRESS BUS
endmodule

module ctrl (
  input  [4:0] OP,
  input  RST,
  input  CLK,
  output DR_DEV,
  output DR_RHS,
  output DR_LHS,
  output DR_MEM,
  output DR_IO,
  output DR_F,
  output DR_K,
  output PC_JNZ,
  output [1:0] AW,
  output [2:0] DW,
  output DW_SEL,
  output DR_SEL,
  output SP_DEC,
  output SP_INC,
  output [2:0] ALU_OP,
  output PC_INC,
  output PC_JMP,
  output FETCH
);

  wire [2:0] counter_1_q;
  wire [5:5] R0_data;
  wire [6:0] R2_data;

  Counter #(.max('h7), .width(3)) counter_1 (
    .clr(RST), .load(R2_data[0]), .up(1'b1), .count(1'b1), .clk(CLK), .D(3'b000), .Q(counter_1_q));  // open: carry
  Hex_Digit_Display #(.decimalPoint("false")) hex_digit_display_1 (.value({1'b0, counter_1_q}));
  ROM R0 (.addr({OP, counter_1_q}), .data({DR_K, DR_F, R0_data[5], DR_IO, DR_MEM, DR_LHS, DR_RHS, DR_DEV}));
  ROM R1 (.addr({OP, counter_1_q}), .data({DR_SEL, DW_SEL, DW, AW, PC_JNZ}));
  ROM R2 (.addr({OP, counter_1_q}), .data({PC_JMP, R2_data[6], ALU_OP, SP_INC, SP_DEC, R2_data[0]}));
  nor nor_1 (FETCH, counter_1_q[0], counter_1_q[1], counter_1_q[2]);
  or or_1 (PC_INC, R2_data[6], FETCH);

  // Notes on the sheet:
  //   contents of R0 (hex, n*v repeats v):
  //   0 4 2 6*0 4 7*0 4 2 40 5*0 4 40 4 2 12*0 4 2 6*0 10 7*0 10 4 2 2 4 0 0 0 2 8 6*0 2 10 4 2 8 0 0 0 2
  //   8 6*0 2 8 6*0 4 15*0 4 2 10 5*0 4 10 6*0 2 10 2 1 4*0 2 10 1 5*0 4 2 2 10 40 0 0 0 4 2 10 40 4*0 4 2
  //   2 10 40 0 0 0 4 2 10 40 4*0 4 2 2 40 4*0 4 2 40 5*0 4 2 2 10 40 0 0 0 4 2 10 40 4*0 4 2 2 10 40 0 0
  //   0 4 2 10 40 4*0 4 2 2 10 40 0 0 0 4 2 10 40 4*0 2 80 6*0 80
  //   contents of R1 (hex, n*v repeats v):
  //   0 8 0 c0 5*0 8 80 6*0 8 0 18 5 4*0 8 18 0 0 7 0 0 0 4 9*0 6 5*0 8 84 6*0 8 0 0 6 28 b8 0 0 8 44 6*0
  //   8 40 0 0 2e 0 0 0 8 42 6*0 8 3a 6*0 8 82 14*0 8 0 40 b0 4*0 8 0 b0 5*0 8 40 0 40 4*0 8 40 6*0 8 0 40
  //   10 18 a8 0 0 8 0 10 18 a8 0 0 0 8 0 40 10 18 a8 0 0 8 0 10 18 a8 0 0 0 8 0 40 18 4*0 8 0 18 5*0 8 0
  //   40 10 18 a8 0 0 8 0 10 18 a8 0 0 0 8 0 40 10 18 a8 0 0 8 0 10 18 a8 0 0 0 8 0 40 10 18 a8 0 0 8 0 10
  //   18 a8 0 0 0 8 40
  //   contents of R2 (hex, n*v repeats v):
  //   0 0 0 41 4*1 0 0 41 5*1 0 0 40 28 4*1 0 0 28 40 40 1 1 1 0 81 6*1 0 40 40 81 4*1 0 0 41 5*1 0 0 40
  //   40 0 0 1 1 0 0 6*1 0 0 0 40 0 41 1 1 0 0 5 5*1 0 0 5 5*1 0 2 6*1 10*0 40 0 4*1 0 0 40 5*1 0 40 0 40
  //   4*1 0 40 0 41 4*1 0 0 40 0 0 0 1 1 0 0 40 0 0 1 1 1 0 0 40 0 8 0 1 1 0 0 40 8 0 1 1 1 0 0 40 0 29 1
  //   1 1 0 0 40 29 4*1 0 0 40 0 10 0 1 1 0 0 40 10 0 1 1 1 0 0 40 0 18 0 1 1 0 0 40 18 0 1 1 1 0 0 40 0
  //   20 0 1 1 0 0 40 20 0 1 1 1 0 40 6*1 0 41 6*1
endmodule

module alu (
  input  [7:0] F_in,
  input  [7:0] A,
  input  [7:0] B,
  input  [2:0] OP,
  output [7:0] Q,
  output [7:0] F
);

  wire ad0_p1, ad1_p1, ad2_p1, and_1_out, and_2_out, and_3_out, and_4_out, and_5_out, and_6_out, and_7_out,
       and_8_out, and_9_out, and_10_out, and_11_out, and_12_out, and_13_out, and_14_out, and_15_out,
       and_16_out, and_17_out, and_18_out, and_19_out, and_20_out, and_21_out, and_22_out, and_23_out,
       and_24_out, bd0_p1, bd1_p1, bd2_p1, BF, CF, demultiplexer_2_out0, demultiplexer_2_out1,
       demultiplexer_2_out5, multiplexer_1_out, nor_1_out, nor_2_out, nor_3_out, nor_4_out, nor_5_out,
       nor_6_out, nor_7_out, nor_8_out, not_1_out, not_2_out, not_3_out, OP_ADD, OP_AND, OP_CMP, OP_NOR,
       OP_OR, OP_SUB, or_1_out, or_2_out, or_3_out, or_4_out, or_5_out, or_6_out, or_7_out, or_8_out,
       or_9_out, or_10_out, or_11_out, or_12_out, or_13_out, or_14_out, or_15_out, or_16_out, or_17_out,
       or_18_out, or_19_out, or_20_out, or_21_out, or_22_out, or_23_out, or_24_out, or_25_out, or_26_out,
       or_27_out, qd0_p1, qd1_p1, qd2_p1, xor_1_out, xor_2_out, xor_3_out, xor_4_out, xor_5_out, xor_6_out,
       xor_7_out, xor_8_out, xor_9_out, xor_10_out, xor_11_out, xor_12_out, xor_13_out, xor_14_out,
       xor_15_out, xor_16_out, xor_17_out, xor_18_out, xor_19_out, xor_20_out, xor_21_out, xor_22_out,
       xor_23_out, xor_24_out, xor_25_out, xor_26_out, xor_27_out, xor_28_out, xor_29_out, xor_30_out,
       xor_31_out, xor_32_out;
  wire [7:0] controlled_buffer_1_out, controlled_buffer_2_out;

  Demultiplexer #(.select(3)) demultiplexer_1 (
    .out0(OP_ADD), .out1(OP_SUB), .out2(OP_AND), .out3(OP_OR), .out4(OP_NOR), .out5(OP_CMP), .in(1'b1),
    .sel(OP));  // open: out6, out7
  or or_1 (or_1_out, OP_ADD, or_3_out);
  or or_2 (or_2_out, OP_ADD, or_3_out);
  assign controlled_buffer_1_out = or_2_out ? B : 8'bz;  // Controlled_Buffer controlled_buffer_1
  assign controlled_buffer_2_out = or_1_out ? A : 8'bz;  // Controlled_Buffer controlled_buffer_2
  or or_3 (or_3_out, OP_SUB, OP_CMP);
  Multiplexer multiplexer_1 (.in0(F_in[2]), .in1(not_1_out), .out(multiplexer_1_out), .sel(or_3_out));
  not not_1 (not_1_out, F_in[3]);
  xor xor_1 (xor_1_out, controlled_buffer_1_out[0], or_3_out);
  xor xor_2 (xor_2_out, or_3_out, controlled_buffer_1_out[1]);
  xor xor_3 (xor_3_out, controlled_buffer_1_out[2], or_3_out);
  xor xor_4 (xor_4_out, or_3_out, controlled_buffer_1_out[3]);
  xor xor_5 (xor_5_out, controlled_buffer_1_out[4], or_3_out);
  xor xor_6 (xor_6_out, or_3_out, controlled_buffer_1_out[5]);
  xor xor_7 (xor_7_out, controlled_buffer_1_out[6], or_3_out);
  xor xor_8 (xor_8_out, or_3_out, controlled_buffer_1_out[7]);
  xor xor_9 (xor_9_out, multiplexer_1_out, controlled_buffer_2_out[0]);
  and and_1 (and_1_out, multiplexer_1_out, controlled_buffer_2_out[0]);
  and and_2 (and_2_out, A[0], B[0]);
  and and_3 (and_3_out, A[1], B[1]);
  and and_4 (and_4_out, A[2], B[2]);
  and and_5 (and_5_out, A[3], B[3]);
  and and_6 (and_6_out, A[4], B[4]);
  and and_7 (and_7_out, A[5], B[5]);
  and and_8 (and_8_out, A[6], B[6]);
  and and_9 (and_9_out, A[7], B[7]);
  xor xor_10 (xor_10_out, xor_9_out, xor_1_out);
  and and_10 (and_10_out, xor_1_out, xor_9_out);
  assign Q[0] = OP_AND ? and_2_out : 1'bz;  // Controlled_Buffer controlled_buffer_3
  assign Q[1] = OP_AND ? and_3_out : 1'bz;  // Controlled_Buffer controlled_buffer_4
  assign Q[2] = OP_AND ? and_4_out : 1'bz;  // Controlled_Buffer controlled_buffer_5
  assign Q[3] = OP_AND ? and_5_out : 1'bz;  // Controlled_Buffer controlled_buffer_6
  assign Q[4] = OP_AND ? and_6_out : 1'bz;  // Controlled_Buffer controlled_buffer_7
  assign Q[5] = OP_AND ? and_7_out : 1'bz;  // Controlled_Buffer controlled_buffer_8
  assign Q[6] = OP_AND ? and_8_out : 1'bz;  // Controlled_Buffer controlled_buffer_9
  assign Q[7] = OP_AND ? and_9_out : 1'bz;  // Controlled_Buffer controlled_buffer_10
  or or_4 (or_4_out, OP_SUB, OP_CMP);
  or or_5 (or_5_out, OP_ADD, or_4_out);
  assign Q[0] = or_5_out ? xor_10_out : 1'bz;  // Controlled_Buffer controlled_buffer_11
  xor xor_11 (xor_11_out, and_1_out, and_10_out);
  xor xor_12 (xor_12_out, xor_11_out, controlled_buffer_2_out[1]);
  and and_11 (and_11_out, xor_11_out, controlled_buffer_2_out[1]);
  or or_6 (or_6_out, OP_SUB, OP_CMP);
  or or_7 (or_7_out, OP_ADD, or_6_out);
  xor xor_13 (xor_13_out, xor_12_out, xor_2_out);
  assign Q[1] = or_7_out ? xor_13_out : 1'bz;  // Controlled_Buffer controlled_buffer_12
  and and_12 (and_12_out, xor_2_out, xor_12_out);
  or or_8 (or_8_out, A[0], B[0]);
  assign Q[0] = OP_OR ? or_8_out : 1'bz;  // Controlled_Buffer controlled_buffer_13
  or or_9 (or_9_out, A[1], B[1]);
  assign Q[1] = OP_OR ? or_9_out : 1'bz;  // Controlled_Buffer controlled_buffer_14
  or or_10 (or_10_out, A[2], B[2]);
  assign Q[2] = OP_OR ? or_10_out : 1'bz;  // Controlled_Buffer controlled_buffer_15
  or or_11 (or_11_out, A[3], B[3]);
  assign Q[3] = OP_OR ? or_11_out : 1'bz;  // Controlled_Buffer controlled_buffer_16
  or or_12 (or_12_out, A[4], B[4]);
  assign Q[4] = OP_OR ? or_12_out : 1'bz;  // Controlled_Buffer controlled_buffer_17
  or or_13 (or_13_out, A[5], B[5]);
  assign Q[5] = OP_OR ? or_13_out : 1'bz;  // Controlled_Buffer controlled_buffer_18
  or or_14 (or_14_out, A[6], B[6]);
  assign Q[6] = OP_OR ? or_14_out : 1'bz;  // Controlled_Buffer controlled_buffer_19
  or or_15 (or_15_out, A[7], B[7]);
  assign Q[7] = OP_OR ? or_15_out : 1'bz;  // Controlled_Buffer controlled_buffer_20
  xor xor_14 (xor_14_out, and_11_out, and_12_out);
  xor xor_15 (xor_15_out, xor_14_out, controlled_buffer_2_out[2]);
  and and_13 (and_13_out, xor_14_out, controlled_buffer_2_out[2]);
  xor xor_16 (xor_16_out, xor_15_out, xor_3_out);
  and and_14 (and_14_out, xor_3_out, xor_15_out);
  or or_16 (or_16_out, OP_SUB, OP_CMP);
  or or_17 (or_17_out, OP_ADD, or_16_out);
  assign Q[2] = or_17_out ? xor_16_out : 1'bz;  // Controlled_Buffer controlled_buffer_21
  xor xor_17 (xor_17_out, and_13_out, and_14_out);
  nor nor_1 (nor_1_out, A[0], B[0]);
  assign Q[0] = OP_NOR ? nor_1_out : 1'bz;  // Controlled_Buffer controlled_buffer_22
  nor nor_2 (nor_2_out, A[1], B[1]);
  assign Q[1] = OP_NOR ? nor_2_out : 1'bz;  // Controlled_Buffer controlled_buffer_23
  nor nor_3 (nor_3_out, A[2], B[2]);
  assign Q[2] = OP_NOR ? nor_3_out : 1'bz;  // Controlled_Buffer controlled_buffer_24
  nor nor_4 (nor_4_out, A[3], B[3]);
  assign Q[3] = OP_NOR ? nor_4_out : 1'bz;  // Controlled_Buffer controlled_buffer_25
  nor nor_5 (nor_5_out, A[4], B[4]);
  assign Q[4] = OP_NOR ? nor_5_out : 1'bz;  // Controlled_Buffer controlled_buffer_26
  nor nor_6 (nor_6_out, A[5], B[5]);
  assign Q[5] = OP_NOR ? nor_6_out : 1'bz;  // Controlled_Buffer controlled_buffer_27
  nor nor_7 (nor_7_out, A[6], B[6]);
  assign Q[6] = OP_NOR ? nor_7_out : 1'bz;  // Controlled_Buffer controlled_buffer_28
  nor nor_8 (nor_8_out, A[7], B[7]);
  assign Q[7] = OP_NOR ? nor_8_out : 1'bz;  // Controlled_Buffer controlled_buffer_29
  xor xor_18 (xor_18_out, xor_17_out, controlled_buffer_2_out[3]);
  and and_15 (and_15_out, xor_17_out, controlled_buffer_2_out[3]);
  or or_18 (or_18_out, OP_SUB, OP_CMP);
  or or_19 (or_19_out, OP_ADD, or_18_out);
  xor xor_19 (xor_19_out, xor_18_out, xor_4_out);
  assign Q[3] = or_19_out ? xor_19_out : 1'bz;  // Controlled_Buffer controlled_buffer_30
  and and_16 (and_16_out, xor_4_out, xor_18_out);
  xor xor_20 (xor_20_out, and_15_out, and_16_out);
  xor xor_21 (xor_21_out, xor_20_out, controlled_buffer_2_out[4]);
  and and_17 (and_17_out, xor_20_out, controlled_buffer_2_out[4]);
  xor xor_22 (xor_22_out, xor_21_out, xor_5_out);
  and and_18 (and_18_out, xor_5_out, xor_21_out);
  or or_20 (or_20_out, OP_SUB, OP_CMP);
  or or_21 (or_21_out, OP_ADD, or_20_out);
  assign Q[4] = or_21_out ? xor_22_out : 1'bz;  // Controlled_Buffer controlled_buffer_31
  xor xor_23 (xor_23_out, and_17_out, and_18_out);
  xor xor_24 (xor_24_out, xor_23_out, controlled_buffer_2_out[5]);
  and and_19 (and_19_out, xor_23_out, controlled_buffer_2_out[5]);
  or or_22 (or_22_out, OP_SUB, OP_CMP);
  or or_23 (or_23_out, OP_ADD, or_22_out);
  xor xor_25 (xor_25_out, xor_24_out, xor_6_out);
  assign Q[5] = or_23_out ? xor_25_out : 1'bz;  // Controlled_Buffer controlled_buffer_32
  and and_20 (and_20_out, xor_6_out, xor_24_out);
  xor xor_26 (xor_26_out, and_19_out, and_20_out);
  xor xor_27 (xor_27_out, xor_26_out, controlled_buffer_2_out[6]);
  and and_21 (and_21_out, xor_26_out, controlled_buffer_2_out[6]);
  xor xor_28 (xor_28_out, xor_27_out, xor_7_out);
  and and_22 (and_22_out, xor_7_out, xor_27_out);
  Demultiplexer #(.select(3)) demultiplexer_2 (
    .out0(demultiplexer_2_out0), .out1(demultiplexer_2_out1), .out5(demultiplexer_2_out5), .in(1'b1), .sel(OP));  // open: out2, out3, out4, out6, out7
  or or_24 (or_24_out, OP_SUB, OP_CMP);
  or or_25 (or_25_out, OP_ADD, or_24_out);
  assign Q[6] = or_25_out ? xor_28_out : 1'bz;  // Controlled_Buffer controlled_buffer_33
  xor xor_29 (xor_29_out, and_21_out, and_22_out);
  xor xor_30 (xor_30_out, xor_29_out, controlled_buffer_2_out[7]);
  and and_23 (and_23_out, xor_29_out, controlled_buffer_2_out[7]);
  or or_26 (or_26_out, OP_SUB, OP_CMP);
  or or_27 (or_27_out, OP_ADD, or_26_out);
  xor xor_31 (xor_31_out, xor_30_out, xor_8_out);
  assign Q[7] = or_27_out ? xor_31_out : 1'bz;  // Controlled_Buffer controlled_buffer_34
  and and_24 (and_24_out, xor_8_out, xor_30_out);
  Multiplexer multiplexer_2 (.in0(F_in[0]), .in1(F[4]), .out(F[0]), .sel(demultiplexer_2_out5));
  Multiplexer multiplexer_3 (.in0(F_in[1]), .in1(BF), .out(F[1]), .sel(demultiplexer_2_out5));
  Multiplexer multiplexer_4 (.in0(F_in[2]), .in1(CF), .out(F[2]), .sel(demultiplexer_2_out0));
  Multiplexer multiplexer_5 (.in0(F_in[3]), .in1(BF), .out(F[3]), .sel(demultiplexer_2_out1));
  nor nor_9 (F[5], A[0], A[1], A[2], A[3], A[5], A[6], A[7], A[4]);
  xor xor_32 (xor_32_out, and_23_out, and_24_out);
  LED LF (.in(F[1]));
  LED u_CF (.in(F[2]));
  LED u_BF (.in(F[3]));
  LED ZF (.in(F[4]));
  not not_2 (not_2_out, or_3_out);
  LED EF (.in(F[0]));
  and and_25 (CF, not_2_out, xor_32_out);
  not not_3 (not_3_out, xor_32_out);
  and and_26 (BF, or_3_out, not_3_out);
  nor nor_10 (F[4], Q[0], Q[1], Q[2], Q[3], Q[4], Q[5], Q[6], Q[7]);
  // _7_Segment_Display qd2: pin names not known; wires that end beside it: qd2_p1, qd2_p1
  // BCD_to_7_Segment_decoder bcd_to_7_segment_decoder_1: pin names not known
  // Binary_to_BCD_converter #(.binvalue(8)) binary_to_bcd_converter_1: pin names not known; wires that end beside it: Q
  // _7_Segment_Display qd1: pin names not known; wires that end beside it: qd1_p1, qd1_p1
  // _7_Segment_Display qd0: pin names not known; wires that end beside it: qd0_p1, qd0_p1
  // BCD_to_7_Segment_decoder bcd_to_7_segment_decoder_2: pin names not known
  // BCD_to_7_Segment_decoder bcd_to_7_segment_decoder_3: pin names not known
  // _7_Segment_Display ad2: pin names not known; wires that end beside it: ad2_p1, ad2_p1
  // BCD_to_7_Segment_decoder bcd_to_7_segment_decoder_4: pin names not known
  // _7_Segment_Display bd2: pin names not known; wires that end beside it: bd2_p1, bd2_p1
  // BCD_to_7_Segment_decoder bcd_to_7_segment_decoder_5: pin names not known
  // _7_Segment_Display ad1: pin names not known; wires that end beside it: ad1_p1, ad1_p1
  // BCD_to_7_Segment_decoder bcd_to_7_segment_decoder_6: pin names not known
  // Binary_to_BCD_converter #(.binvalue(8)) binary_to_bcd_converter_2: pin names not known; wires that end beside it: A
  // _7_Segment_Display bd1: pin names not known; wires that end beside it: bd1_p1, bd1_p1
  // BCD_to_7_Segment_decoder bcd_to_7_segment_decoder_7: pin names not known
  // Binary_to_BCD_converter #(.binvalue(8)) binary_to_bcd_converter_3: pin names not known; wires that end beside it: B
  // _7_Segment_Display ad0: pin names not known; wires that end beside it: ad0_p1, ad0_p1
  // BCD_to_7_Segment_decoder bcd_to_7_segment_decoder_8: pin names not known
  // _7_Segment_Display bd0: pin names not known; wires that end beside it: bd0_p1, bd0_p1
  // BCD_to_7_Segment_decoder bcd_to_7_segment_decoder_9: pin names not known

  assign F[7:6] = 2'b00;

  // Other names for the same wires on the sheet: ZF = F[4]; F_t[7:0] = F_in
endmodule

module mem (
  input  [15:0] ADDR,
  input  WE,
  input  CLK,
  input  [7:0] D_in,
  output [7:0] D_Out
);

  wire [7:0] ram_1_dout, rom_1_data;

  RAM #(.addrWidth(15), .enables("line")) ram_1 (.addr(ADDR[14:0]), .we(WE), .clk(CLK), .din(D_in), .dout(ram_1_dout));
  ROM #(.addrWidth(15)) rom_1 (.addr(ADDR[14:0]), .data(rom_1_data));
  Multiplexer #(.width(8)) multiplexer_1 (.in0(rom_1_data), .in1(ram_1_dout), .out(D_Out), .sel(ADDR[15]));

  // Notes on the sheet:
  //   contents of rom_1 (hex, n*v repeats v):
  //   cf b 98 1 99 0 28
endmodule

module dev_kb (
  input  CLK,
  input  SEND,
  input  RECV,
  input  [7:0] MOSI,
  output [7:0] MISO
);

  wire keyboard_1_avail;

  Keyboard keyboard_1 (.clk(CLK), .re(SEND), .clr(RECV), .avail(keyboard_1_avail), .data(MISO[6:0]));
  not not_1 (MISO[7], keyboard_1_avail);
endmodule

module dev_rng (
  input  CLK,
  input  SEND,
  input  RECV,
  input  [7:0] MOSI,
  output [7:0] MISO
);

  Random random_1 (.clr(RECV), .next(SEND), .clk(CLK), .out(MISO));
endmodule

module ic (
);

  wire n74245_1_pin1, n74245_1_pin19, n74377_1_pin1, n74377_1_pin2, n74377_1_pin5, n74377_1_pin6,
       n74377_1_pin9, n74377_1_pin11, n74377_1_pin12, n74377_1_pin15, n74377_1_pin16, n74377_1_pin19;
  wire [7:0] n74377_1_pin3;

  _74377 u_74377_1 (
    .pin1(n74377_1_pin1), .pin2(n74377_1_pin2), .pin3(n74377_1_pin3[0]), .pin4(n74377_1_pin3[1]),
    .pin5(n74377_1_pin5), .pin6(n74377_1_pin6), .pin7(n74377_1_pin3[2]), .pin8(n74377_1_pin3[3]),
    .pin9(n74377_1_pin9), .pin19(n74377_1_pin19), .pin18(n74377_1_pin3[7]), .pin17(n74377_1_pin3[6]),
    .pin16(n74377_1_pin16), .pin15(n74377_1_pin15), .pin14(n74377_1_pin3[5]), .pin13(n74377_1_pin3[4]),
    .pin12(n74377_1_pin12), .pin11(n74377_1_pin11));
  _74245 u_74245_1 (
    .pin1(n74245_1_pin1), .pin2(n74377_1_pin2), .pin3(n74377_1_pin5), .pin4(n74377_1_pin6),
    .pin5(n74377_1_pin9), .pin6(n74377_1_pin12), .pin7(n74377_1_pin15), .pin8(n74377_1_pin16),
    .pin9(n74377_1_pin19), .pin19(n74245_1_pin19), .pin18(n74377_1_pin3[0]), .pin17(n74377_1_pin3[1]),
    .pin16(n74377_1_pin3[2]), .pin15(n74377_1_pin3[3]), .pin14(n74377_1_pin3[4]), .pin13(n74377_1_pin3[5]),
    .pin12(n74377_1_pin3[6]), .pin11(n74377_1_pin3[7]));
  assign n74377_1_pin3 = 1'b0 ? 8'h3 : 8'bz;  // Controlled_Buffer controlled_buffer_1
  // also tied to GND on the sheet: n74245_1_pin19
  // also tied to VCC on the sheet: {n74377_1_pin1, n74377_1_pin11, n74245_1_pin1}
endmodule

module byte_display (
  input  [7:0] in_1
);

  wire d0_p1, d1_p1, d2_p1;

  // _7_Segment_Display d2: pin names not known; wires that end beside it: d2_p1, d2_p1
  // _7_Segment_Display d1: pin names not known; wires that end beside it: d1_p1, d1_p1
  // BCD_to_7_Segment_decoder bcd_to_7_segment_decoder_1: pin names not known
  // BCD_to_7_Segment_decoder bcd_to_7_segment_decoder_2: pin names not known
  // Binary_to_BCD_converter #(.binvalue(8)) binary_to_bcd_converter_1: pin names not known; wires that end beside it: in_1
  // _7_Segment_Display d0: pin names not known; wires that end beside it: d0_p1, d0_p1
  // BCD_to_7_Segment_decoder bcd_to_7_segment_decoder_3: pin names not known
endmodule
